# Fritzing sketch Main_unit (saved by Fritzing 0.9.3b)

parts:
  U1 = 74HC595 [package="DIP16 [THT]"]
  U2 = Mini-360 DC-DC Buck converter [package=THT]
  U3 = LM2596 step down module  # not connected
  BAT1 = 12 battery [package=battery]
  U5 = RELAY-SOLIDSTATE [package=relay-s108t02]
  A1 = 2 channel relay module [package=THT]
  J1 = Piezo Speaker
  Analog = FTDI_BASIC [package=ftdi_basic]
  hc-sr1 = hc-sr04
  hc-sr2 = hc-sr04
  U6 = RELAY-SOLIDSTATE [package=relay-s108t02]
  U7 = RELAY-SOLIDSTATE [package=relay-s108t02]
  U8 = RELAY-SOLIDSTATE [package=relay-s108t02]
  Digital = FTDI_BASIC [package=ftdi_basic]
  YF-S201_Flow_Meter1 = YF-S201 Water Flow Meter
  C1 = Capacitor [package=cap-pth-small2]
  C2 = Capacitor [package=cap-pth-small2]
  C3 = Capacitor [package=cap-pth-small2]
  U9 = ESP32-38PinWide [part_number=ESP32-38PinWide]
  R3 = Resistor [tolerance=±5% resistance=6.7k package=THT]
  R4 = Resistor [tolerance=±5% resistance=6.7k package=THT]
  R6 = Resistor [tolerance=±5% resistance=6.7k package=THT]
  R7 = Resistor [tolerance=±5% resistance=1k package=THT]
  F1 = FUSE [package=fuse_5mm]
  D1 = Zener Diode [part_number=1N4732A breakdown_voltage=3.6V package="Melf DO-213 AB [SMD]"]  # not connected

nets:
  N1: U1.Q1, A1.pin_9
  N2: U1.Q2, A1.pin_12
  N3: U1.Q3, U7.+
  N4: U1.Q4, U5.+
  N5: U1.Q5, U8.+
  N6: U1.Q6, U6.+
  N7: U1.Q7, J1.pin2
  N8: U1.GND, U5.-
  VCC: U1.MR, U1.VCC, YF-S201_Flow_Meter1.VCC, U9.VIN, F1.2
  N9: U1.SH_CP, U9.GPIO16
  N10: U1.ST_CP, U9.GPIO4
  GND: U1.OE, U2.OUT-, J1.pin1, hc-sr1.GND, hc-sr2.GND, U6.-, U7.-, U8.-, YF-S201_Flow_Meter1.GND, C1.2, C2.2, C3.2, U9.GND
  N11: U1.DS, U9.GPIO0
  N12: U2.IN-, BAT1.-, R7.Pin_1
  N13: U2.IN+, BAT1.+, R6.Pin_0
  N14: U2.OUT+, F1.1
  N15: Analog.5, U9.GPIO33, R6.Pin_1, R7.Pin_0
  N16: Analog.1, U9.GPIO32
  N17: Analog.6, U9.GPIO35
  N18: Analog.2, U9.GPIO34
  N19: Analog.3, U9.GPIO39, R3.Pin_0
  N20: Analog.4, U9.GPIO36, R4.Pin_0
  VCC_2: hc-sr1.VCC, hc-sr2.VCC
  N21: hc-sr1.Trig, hc-sr2.Trig, U9.GPIO21
  N22: hc-sr1.Echo, C1.1, U9.GPIO19
  N23: hc-sr2.Echo, C2.1, U9.GPIO18
  N24: Digital.5, U9.GPIO25
  N25: Digital.1, U9.GPIO26
  N26: Digital.6, U9.GPIO23
  N27: Digital.2, U9.GPIO22
  N28: Digital.3, U9.GPIO14
  N29: Digital.4, U9.GPIO27
  N30: YF-S201_Flow_Meter1.SIG, C3.1, U9.GPIO13
  N31: U9.3.3, R3.Pin_1, R4.Pin_1

custom parts:
  Mini-360 DC-DC Buck converter: Mini-360 DC-DC Buck converter. Tiny buck step down voltage converter, input voltage 4.75 to 23V output 1 to 17V adjustable. Available from ebay and the like.
  LM2596 step down module: LM2596 DC-DC step down power supply module 3 A.
  12 battery: 12V lead acid type battery, like the Husqvarna YTH2448 12V 35AH battery. This is the mini version 1/4 the size of the actual battery to be closer to typical breadboard parts (around 2in wide rathher than 7in). The pads in pcb are sized to accomidate up to 14ga wire (as these batterys will deliver high currents.)
  2 channel relay module: 2 channel Relay Module 5V 12V 24V High and Low Level Trigger Relay Control With Optocoupler Two Way relays DC 5 V 12 V 24 V Volt.
  YF-S201 Water Flow Meter: The YF-S201 Flow Meter. The input voltage is 5V to 24V (DC).
  ESP32-38PinWide: Generic 38-Pin ESP32 with wide format (only access to one side of pins on a breadboard) based on Stephen Lilley's HiLetgo ESP-WROOM-32 ESP32 ESP-32S Development Board.
