# Fritzing sketch esp32_parallel_touchscreen (saved by Fritzing 0.9.3b)
circuit board: 9.56484cm x 7.03106cm

parts:
  R1 = Resistor [tolerance=±5% resistance=1k package=THT]
  R2 = Resistor [tolerance=±10% resistance=5.1k package=THT]
  U2 = Header 1 [package=1x01_offset]
  U3 = Header 1 [part_number=GND package=1x01_offset]
  U4 = Header 1 [package=1x01_offset]
  U5 = Header 1 [package=1x01_offset]
  U6 = Header 1 [package=1x01_offset]
  U7 = Header 1 [package=1x01_offset]
  U9 = Header 1 [package=1x01_offset]
  U10 = Header 1 [package=1x01_offset]
  R3 = Resistor [tolerance=±10% resistance=5.1k package=THT]
  R4 = Resistor [tolerance=±10% resistance=5.1k package=THT]
  U11 = Header 1 [package=1x01_offset]
  U12 = Header 1 [package=1x01_offset]
  U13 = Header 1 [package=1x01_offset]
  U14 = Header 1 [package=1x01_offset]
  M1 = DOIT Esp32 DevKit v1 (30 pins long, 11 pins width) [part_number=ESP32S-PIN30]
  Componente1 = Arduino Uno (Rev3) - ICSP
  Componente2 = Thumb Joystick
  Componente3 = Arduino Uno (Rev3) - ICSP
  S1 = Square Pushbutton
  S2 = Square Pushbutton

nets:
  N1: R1.Pin_0, M1.D14
  N2: R1.Pin_1, U4.1, Componente3.D0/RX
  N3: R2.Pin_0, M1.VP
  N4: R2.Pin_1, M1.D25, Componente1.A2
  N5: U2.1, M1.D12, Componente3.D1/TX
  GND: U3.1, U7.1, U12.1, U14.1, M1.GND, Componente1.GND, Componente2.GND, Componente3.GND, S1.leg0, S2.leg0
  3V3: U5.1, R3.Pin_1, M1.3V3, Componente2.VCC
  N6: U6.1, M1.D32
  N7: U9.1, M1.D34, Componente2.HORZ
  N8: U10.1, M1.VN, Componente2.VERT
  N9: R3.Pin_0, R4.Pin_1, U13.1, M1.D35, S1.leg1
  N10: R4.Pin_0, U11.1, S2.leg1
  N11: M1.D15, Componente1.D3_PWM
  N12: M1.D2, Componente1.A1
  N13: M1.D4, Componente1.A0
  N14: M1.RX2, Componente1.D5_PWM
  N15: M1.TX2, Componente1.D4
  N16: M1.D5, Componente1.D10_PWM/SS
  N17: M1.D18, Componente1.D13/SCK
  N18: M1.D19, Componente1.D12/MISO
  N19: M1.D21, Componente1.D8
  N20: M1.D22, Componente1.D7
  N21: M1.D23, Componente1.D11_PWM/MOSI
  N22: M1.EN, Componente1.A4/SDA
  N23: M1.D33, Componente1.A3
  N24: M1.D26, Componente1.D9_PWM
  N25: M1.D27, Componente1.D6_PWM
  N26: M1.D13, Componente1.D2
  VIN: M1.VIN, Componente1.5V

notes:
  GRBL controller

custom parts:
  DOIT Esp32 DevKit v1 (30 pins long, 11 pins width): The DOIT Esp32 DevKit v1 is one of the development board created by DOIT to evaluate the ESP-WROOM-32 module. It is based on the ESP32 microcontroller that boasts Wifi, Bluetooth, Ethernet and Low Power support all in a single chip. (vanepp) made breadboard work, adjusted pin numbering and labels and reduced size of schematic and cleaned up pcb. This chip is 30pins long (2 x15) and 11 pins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
